# Fritzing sketch bms (saved by Fritzing 0.9.4)
breadboards: 1

parts:
  Part1 = Arduino MKR1000
  U1 = LIPO-2000mAh [package=lipo-2000]
  Part2 = Adafruit ADS1115 16Bit I2C ADC [part_number="Adafruit #1085"]
  Part3 = NeoPixel Stick [part_number=1426]
  R1 = Resistor [tolerance=±5% resistance=247 package=THT]

nets:
  N1: Part1.D11_SDA, Part2.SDA
  N2: Part1.D12_SCL, Part2.SCL
  5V: Part1.5V, Part2.VDD, Part3.+5V
  N3: U1.+, Part2.AIN0
  GND: U1.-, Part2.GND, Part3.GND
  N4: Part3.DATAIN, R1.Pin_1

custom parts:
  Arduino MKR1000: MKR1000 is a powerful board that combines the functionality of the Zero and the Wi-Fi Shield. It is the ideal solution for makers wanting to design IoT projects with minimal previous experience in networking
  Adafruit ADS1115 16Bit I2C ADC: For microcontrollers without an analog-to-digital converter or when you want a higher-precision ADC, the ADS1115 provides 16-bit precision at 860 samples/second over I2C. The chip can be configured as 4 single-ended input channels, or two differential channels. As a nice bonus, it even includes a programmable gain amplifier, up to x16, to help boost up smaller single/differential signals to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
  NeoPixel Stick: Make your own little LED strip arrangement with this stick of NeoPixel LEDs. We crammed 8 of the tiny 5050 (5mm x 5mm) smart RGB LEDs onto a PCB with mounting holes and a chainable design. Use only one microcontroller pin to control as many as you can chain together! Each LED is addressable as the driver chip is inside the LED. Each one has ~18mA constant current drive so the color will be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
